# Fritzing sketch nano_test (saved by Fritzing 0.9.0b)
breadboards: 1

parts:
  Part1 = Arduino Nano (Rev3.0)
  LED2 = LED - 5mm [color="White (4500K)" package="5 mm [THT]"]
  LED3 = LED - 5mm [color="Blue (470nm)" package="5 mm [THT]"]
  R2 = Resistor [tolerance=±5% resistance=470 package=THT]
  R3 = Resistor [tolerance=±5% resistance=470 package=THT]
  R4 = Resistor [tolerance=±5% resistance=470 package=THT]
  R5 = Resistor [tolerance=±5% resistance=470 package=THT]
  R6 = Resistor [tolerance=±5% resistance=470 package=THT]
  LED4 = LED - 5mm [color="Green (555nm)" package="5 mm [THT]"]
  LED5 = LED - 5mm [color="Yellow (595nm)" package="5 mm [THT]"]
  LED6 = LED - 5mm [color="Red (633nm)" package="5 mm [THT]"]

nets:
  N1: Part1.GND, LED2.cathode, LED3.cathode, LED4.cathode, LED5.anode, LED6.anode
  N2: Part1.D8, R6.Pin_0
  N3: Part1.D9, R5.Pin_0
  N4: Part1.D10, R4.Pin_0
  N5: Part1.D11/MOSI, R2.Pin_0
  N6: Part1.D12/MISO, R3.Pin_0
  N7: LED2.anode, R3.Pin_1
  N8: LED3.anode, R2.Pin_1
  N9: R4.Pin_1, LED4.anode
  N10: R5.Pin_1, LED5.cathode
  N11: R6.Pin_1, LED6.cathode

notes:
  Resistors = 470Ohms;
  Long led of LED is positive
